# Fritzing sketch buss (saved by Fritzing 0.8.0b)
perfboards: 1

parts:
  J1 = Piezo Speaker
  Part1 = Arduino Uno (Rev3)  # not connected
  J2 = shrouded pin header, 10 pins [form="♂ (shrouded male)"]
  S1 = Tilt Switch [package=THT]
  R2 = Resistor [tolerance=±5% resistance=15k package=THT]
  R1 = Resistor [tolerance=±5% resistance=100 package=THT]
  Q1 = PNP-Transistor [package="TO92 [THT]"]

nets:
  N1: J1.pin1, J2.pin5
  N2: J1.pin2, R1.Pin_1
  N3: J2.pin3, R2.Pin_1
  N4: J2.pin4, S1.Pin_1
  N5: J2.pin6, R1.Pin_0
  N6: J2.pin8, Q1.C
  N7: J2.pin9, Q1.B
  N8: J2.pin10, Q1.E
  N9: S1.Pin_2, R2.Pin_0
